# Fritzing sketch TB10-L3 (saved by Fritzing 1.0.5)
breadboards: 1

parts:
  JP1 = Tk Driver Motor [package=1x06-smd]
  M1 = MOTOR LOZ
  esp1 = ESP32 DevKitc V4
  LED1 = smd LED [color="Red (633nm)" package="0603 [SMD]"]
  U1 = POT [knob_status=50% power=0.5W package=alps_pot]
  R1 = Photocell (LDR) [power=0.25W dark_resistance_@0.01lx=300kΩ light_resistance_@100lx=400Ω luminance=10lx package=THT]
  R2 = Resistor [tolerance=±5% resistance=220 package="0805 [SMD]"]

nets:
  N1: JP1.A, esp1.IO18
  N2: JP1.B, esp1.IO19
  N3: JP1.MOTOR1, M1.VCC
  N4: JP1.MOTOR2, M1.GND
  N5: esp1.GND, esp1.IO35, U1.A, R1.pin_1, R2.Pin_0
  N6: esp1.3V3, U1.E, R1.pin_0
  N7: esp1.IO34, U1.S
  N8: esp1.IO26, LED1.anode
  N9: LED1.cathode, R2.Pin_1

custom parts:
  Tk Driver Motor: Header 6 Standard 6-pin 0.1 header. Use with straight break away headers (SKU : PRT-00116), right angle break away headers (PRT-00553), swiss pins (PRT-00743), machine pins (PRT-00117), and female headers (PRT-00115). Molex polarized connector foot print use with SKU : PRT-08094 with associated crimp pins and housings. NOTES ON THE VARIANTS LOCK and LOCK_LONGPADS... This footprint was designed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
  MOTOR LOZ: Generic gear motor, 3V to 6V, dual output shafts, 1:48 gear ratio.
  ESP32 DevKitc V4: ESP32-DevKitC board with ESP32-WROOM-32 module. ESP32-DevKitC V4 is a small-sized ESP32-based development board produced by Espressif. Most of the pins on the ESP module are broken out to the pin headers on the board. The pins D0, D1, D2, D3, CMD and CLK are used internally for communication between ESP32 and SPI flash memory. They are grouped on both sides near the USB connector. Avoid using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
