# Fritzing sketch TB10-L5 (saved by Fritzing 1.0.5)
breadboards: 1

parts:
  JP1 = Tk Driver Motor [package=1x06-smd]
  M1 = MOTOR LOZ
  esp1 = ESP32 DevKitc V4
  LED1 = smd LED [color="Blue (525nm)" package="0603 [SMD]"]
  R2 = Resistor [tolerance=±5% resistance=1k package="0805 [SMD]"]
  R3 = Resistor [tolerance=±5% resistance=1k package="0805 [SMD]"]
  LED2 = smd LED [color="Green (570nm)" package="0603 [SMD]"]
  R4 = Resistor [tolerance=±5% resistance=1k package="0805 [SMD]"]
  LED3 = smd LED [color="Yellow (595nm)" package="0603 [SMD]"]
  R5 = Resistor [tolerance=±5% resistance=1k package="0805 [SMD]"]
  LED4 = smd LED [color="Orange (620nm)" package="0603 [SMD]"]
  U1 = POT [knob_status=50% power=0.5W package=alps_pot]

nets:
  N1: JP1.A, esp1.IO18
  N2: JP1.B, esp1.IO19
  N3: JP1.MOTOR1, M1.VCC
  N4: JP1.MOTOR2, M1.GND
  N5: esp1.GND, R2.Pin_0, R3.Pin_0, R4.Pin_0, R5.Pin_0, U1.A
  N6: esp1.3V3, U1.E
  N7: esp1.IO34, U1.S
  N8: esp1.IO33, LED4.anode
  N9: esp1.IO27, LED3.anode
  N10: esp1.IO14, LED2.anode
  N11: esp1.IO13, LED1.anode
  N12: LED1.cathode, R2.Pin_1
  N13: R3.Pin_1, LED2.cathode
  N14: R4.Pin_1, LED3.cathode
  N15: R5.Pin_1, LED4.cathode

custom parts:
  Tk Driver Motor: Header 6 Standard 6-pin 0.1 header. Use with straight break away headers (SKU : PRT-00116), right angle break away headers (PRT-00553), swiss pins (PRT-00743), machine pins (PRT-00117), and female headers (PRT-00115). Molex polarized connector foot print use with SKU : PRT-08094 with associated crimp pins and housings. NOTES ON THE VARIANTS LOCK and LOCK_LONGPADS... This footprint was designed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
  MOTOR LOZ: Generic gear motor, 3V to 6V, dual output shafts, 1:48 gear ratio.
  ESP32 DevKitc V4: ESP32-DevKitC board with ESP32-WROOM-32 module. ESP32-DevKitC V4 is a small-sized ESP32-based development board produced by Espressif. Most of the pins on the ESP module are broken out to the pin headers on the board. The pins D0, D1, D2, D3, CMD and CLK are used internally for communication between ESP32 and SPI flash memory. They are grouped on both sides near the USB connector. Avoid using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
