# Fritzing sketch TB10-L8 (saved by Fritzing 1.0.5)
breadboards: 1

parts:
  JP1 = Tk Driver Motor [package=1x06-smd]
  M1 = MOTOR LOZ
  esp1 = ESP32 DevKitc V4
  HC-SR04_Sensor_1 = HC-SR04 Ultrasonic Distance Sensor
  R1 = Resistor [tolerance=±5% resistance=1k package="0805 [SMD]"]
  LED1 = smd LED [color="Red (633nm)" package="1206 [SMD]"]
  J1 = Basic Servo

nets:
  N1: JP1.A, esp1.IO18
  N2: JP1.B, esp1.IO19
  N3: JP1.MOTOR1, M1.VCC
  N4: JP1.MOTOR2, M1.GND
  N5: esp1.IO4, HC-SR04_Sensor_1.TRIG
  N6: esp1.IO5, HC-SR04_Sensor_1.ECHO
  N7: esp1.IO23, J1.pulse
  GND: esp1.GND, HC-SR04_Sensor_1.GND, R1.Pin_0, J1.gnd
  VCC: esp1.3V3, HC-SR04_Sensor_1.VCC, J1.vcc
  N8: esp1.IO26, LED1.anode
  N9: R1.Pin_1, LED1.cathode

custom parts:
  Tk Driver Motor: Header 6 Standard 6-pin 0.1 header. Use with straight break away headers (SKU : PRT-00116), right angle break away headers (PRT-00553), swiss pins (PRT-00743), machine pins (PRT-00117), and female headers (PRT-00115). Molex polarized connector foot print use with SKU : PRT-08094 with associated crimp pins and housings. NOTES ON THE VARIANTS LOCK and LOCK_LONGPADS... This footprint was designed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
  MOTOR LOZ: Generic gear motor, 3V to 6V, dual output shafts, 1:48 gear ratio.
  ESP32 DevKitc V4: ESP32-DevKitC board with ESP32-WROOM-32 module. ESP32-DevKitC V4 is a small-sized ESP32-based development board produced by Espressif. Most of the pins on the ESP module are broken out to the pin headers on the board. The pins D0, D1, D2, D3, CMD and CLK are used internally for communication between ESP32 and SPI flash memory. They are grouped on both sides near the USB connector. Avoid using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
